# Fritzing sketch squema (saved by Fritzing 0.9.6b)

parts:
  Part1 = Breadboard Power Supply Board SMD
  U1 = ESP8266 NodeMCU LoLin module
  L298N1 = L298N DC motor driver
  M1 = DC Motor
  M2 = DC Motor
  VCC1 = Battery block 9V
  KY-1 = Keyes Relay [package=THT]
  M4 = DC Motor
  M3 = DC Motor

nets:
  N1: Part1.GND, KY-1.C
  VCC: Part1.VCC, U1.Vin, M4.pin_2
  N2: U1.D0, L298N1.ENB
  N3: U1.D1, L298N1.IN4
  N4: U1.D2, L298N1.IN3
  N5: U1.D3, L298N1.IN2
  N6: U1.D4, L298N1.IN1
  N7: U1.D5, L298N1.ENA
  N8: U1.D6, KY-1.signal
  N9: L298N1.OUT1, M2.pin_2
  N10: L298N1.OUT2, M2.pin_1
  N11: L298N1.OUT3, M1.pin_2
  N12: L298N1.OUT4, M1.pin_1
  N13: L298N1.GND, VCC1.-
  N14: KY-1.NO, M4.pin_1, M3.pin_1

notes:
  12v
  WEAPON
  CAR

custom parts:
  ESP8266 NodeMCU LoLin module: ESP8266 based NodeMCU
  L298N DC motor driver: 2x DC motor driver with 78M05 positive voltage regulator (7..35 V) L298N: max 46 V, 2 A Set 5 V Enable jumper to enable 5 V regultor (needed for the L298N) and +5 V output at screw terminal or supply external +5 V at screw terminal Set ENA and/or ENB to +5 V to enable motor permanently or supply ENA and/or ENB with PWM signal IN1 and IN2 set rotation directory for motor A (OUT1/OUT2) IN2 and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
  Keyes Relay: The Keyes 5V relay module is suitable for SCM development, home appliance control. It uses a 5V~12V TIL control signal which can control DC / AC signal.
